# Fritzing sketch Car LED Controller (saved by Fritzing 0.9.10b)
breadboards: 2

parts:
  C1 = Capacitor [package=cap-pth-small2]
  C2 = Capacitor [package=cap-pth-small2]
  C3 = Capacitor [package=cap-pth-small2]
  C4 = Capacitor [package=cap-pth-small2]
  S2 = Momentary Switch [package=ksa_sealed_tac_switch]
  M1 = RioRand LM2596
  M2 = RioRand LM2596
  JP1 = Header 4 [package=molex-1x4_lock]
  U6 = SK6812 RGBW LED Strip
  R11 = Resistor [tolerance=±5% power=0.25 resistance=47k package=THT]
  R12 = Resistor [tolerance=±5% power=0.25 resistance=47k package=THT]
  R13 = Resistor [tolerance=±5% power=0.25 resistance=47k package=THT]
  R14 = Resistor [tolerance=±5% power=0.25 resistance=47k package=THT]
  R15 = Resistor [tolerance=±5% power=0.25 resistance=1M package=THT]
  R16 = Resistor [tolerance=±5% power=0.25 resistance=1M package=THT]
  R17 = Resistor [tolerance=±5% power=0.25 resistance=1M package=THT]
  R18 = Resistor [tolerance=±5% power=0.25 resistance=1M package=THT]
  Power_plug1 = Power plug
  M3 = DOIT Esp32 DevKit v1 (30 pins long, 11 pins width) [part_number=ESP32S-PIN30]
  Part1 = Logic Level Converter
  Part2 = LCD1602-I2C
  U7 = 2-Channel 5v Relay Shield [package=relay-2ch5v10a]

nets:
  GND: C1.1, C2.1, C3.1, C4.1, S2.1, S2.2, M1.Pin_4, M2.Pin_4, U6.GND#0, R11.Pin_0, R12.Pin_0, R13.Pin_0, R14.Pin_0, M3.GND, Part1.GND, Part2.GND, U7.GND
  N1: C1.2, R14.Pin_1, R18.Pin_0, M3.D35
  N2: C2.2, R11.Pin_1, R17.Pin_0, M3.VP
  N3: C3.2, R12.Pin_1, R15.Pin_0, M3.VN
  N4: C4.2, R13.Pin_1, R16.Pin_0, M3.D34
  N5: S2.3, S2.4
  N6: M1.Pin_1, M2.Pin_1, Power_plug1.VCC
  N7: M1.Pin_2, M2.Pin_2, Power_plug1.GND
  N8: M1.Pin_3, U7.K1-In
  VCC: M2.Pin_3, M3.VIN, Part1.HV, Part2.VCC, U7.VCC
  N9: JP1.1, R17.Pin_1
  N10: JP1.2, R15.Pin_1
  N11: JP1.3, R16.Pin_1
  N12: JP1.4, R18.Pin_1
  N13: U6.Din, U6.GND#3, Part1.RX_HV
  N14: U6.+5V#2, U7.K1-On
  N15: M3.3V3, Part1.LV
  N16: M3.D21, Part1.RX2_LV
  N17: M3.D22, Part1.TX2_LV
  N18: M3.D14, Part1.TX_LV
  N19: M3.D13, Part1.RX_LV
  N20: Part1.TX_HV, U7.IN1
  N21: Part1.RX2_HV, Part2.SCL
  N22: Part1.TX2_HV, Part2.SDA

custom parts:
  SK6812 RGBW LED Strip: SK6812 RGBW Strip
  DOIT Esp32 DevKit v1 (30 pins long, 11 pins width): The DOIT Esp32 DevKit v1 is one of the development board created by DOIT to evaluate the ESP-WROOM-32 module. It is based on the ESP32 microcontroller that boasts Wifi, Bluetooth, Ethernet and Low Power support all in a single chip. (vanepp) made breadboard work, adjusted pin numbering and labels and reduced size of schematic and cleaned up pcb. This chip is 30pins long (2 x15) and 11 pins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
  LCD1602-I2C: A standard character display, usually with 2x16 characters. Comes in many colors with LCM1602 IIC attached.
  2-Channel 5v Relay Shield: 2 Channel 5v Relay Shield w. 2x SPD-06VDC-SD-C
